// Logisim project Project 2.circ as structural Verilog: 7 circuits, main circuit main
module main (
);

  wire cin, clock_1_out, control_unit_1_a_enable, control_unit_1_b_enable, control_unit_1_branch,
       control_unit_1_out, control_unit_1_t0, control_unit_1_t1, control_unit_1_t2, not_1_out, RD, str, Zero;
  wire [1:0] control_unit_1_a_select, control_unit_1_b_select, selector;
  wire [2:0] opcode;
  wire [7:0] address, alu_1_result, ram_2_data, registers_1_a, registers_1_b, registers_1_buffer,
       registers_1_pc;
  wire [11:0] ram_1_data;

  CONTROL_UNIT control_unit_1 (
    .opcode(opcode), .RD(RD), .Address(address), .Zero(Zero), .T0(control_unit_1_t0),
    .A_select(control_unit_1_a_select), .A_enable(control_unit_1_a_enable),
    .B_select(control_unit_1_b_select), .B_enable(control_unit_1_b_enable), .Branch(control_unit_1_branch),
    .str(str), .ALU_select(selector), .cin(cin), .out(control_unit_1_out), .T1(control_unit_1_t1),
    .T2(control_unit_1_t2));
  ALU alu_1 (
    .CIN(cin), .B0(registers_1_b[0]), .B1(registers_1_b[1]), .B2(registers_1_b[2]), .B3(registers_1_b[3]),
    .B4(registers_1_b[4]), .B5(registers_1_b[5]), .B6(registers_1_b[6]), .B7(registers_1_b[7]),
    .A0(registers_1_a[0]), .A1(registers_1_a[1]), .A2(registers_1_a[2]), .A3(registers_1_a[3]),
    .A4(registers_1_a[4]), .A5(registers_1_a[5]), .A6(registers_1_a[6]), .A7(registers_1_a[7]),
    .selector(selector), .shift(RD), .result(alu_1_result), .Zero(Zero));
  Registers registers_1 (
    .data(ram_2_data), .result(alu_1_result), .A_select(control_unit_1_a_select),
    .A_enable(control_unit_1_a_enable), .B_select(control_unit_1_b_select),
    .B_enable(control_unit_1_b_enable), .instruction(ram_1_data), .branch(control_unit_1_branch),
    .T1(control_unit_1_t1), .A(registers_1_a), .B(registers_1_b), .address(address), .RD(RD),
    .opcode(opcode), .OUT(control_unit_1_out), .buffer(registers_1_buffer), .TO(control_unit_1_t0),
    .T2(control_unit_1_t2), .pc(registers_1_pc));
  // Probe on registers_1_b
  RAM #(.dataWidth(12)) ram_1 (.addr(registers_1_pc), .data(ram_1_data));  // open: sel, clk, ld, clr
  RAM ram_2 (.addr(address), .data(ram_2_data), .clk(clock_1_out), .ld(not_1_out));  // open: sel, clr
  Clock clock_1 (.out(clock_1_out));
  not not_1 (not_1_out, str);
  assign ram_2_data = str ? registers_1_a : 8'bz;  // Controlled_Buffer controlled_buffer_1
  // Probe on registers_1_a
  TTY #(.trigger("falling")) tty_1 (.data(registers_1_buffer[6:0]), .clk(control_unit_1_out));  // open: we, clr
endmodule

module CONTROL_UNIT (
  input  [2:0] opcode,
  input  RD,
  input  Zero,
  input  [7:0] Address,
  output T0,
  output T1,
  output T2,
  output [1:0] A_select,
  output A_enable,
  output [1:0] B_select,
  output B_enable,
  output Branch,
  output str,
  output [1:0] ALU_select,
  output cin,
  output out
);

  wire and_3_out, and_4_out, clock_1_out, decoder_1_out0, decoder_1_out5, decoder_1_out6,
       demultiplexer_1_out0, demultiplexer_1_out1, demultiplexer_2_out0, demultiplexer_2_out1,
       indirect_1_clear, or_1_out, or_2_out, or_3_out, or_4_out, str_t;
  wire [0:0] decoder_1_out2;
  wire [1:0] counter_1_q, decoder_1_out1;

  Clock clock_1 (.out(clock_1_out));
  Counter #(.width(2), .max('h2)) counter_1 (
    .Q(counter_1_q), .clk(clock_1_out), .clr(indirect_1_clear));  // open: load, D, count, carry
  Demultiplexer demultiplexer_1 (
    .out0(demultiplexer_1_out0), .out1(demultiplexer_1_out1), .in(decoder_1_out0), .sel(RD));  // open: en
  Demultiplexer demultiplexer_2 (
    .out0(demultiplexer_2_out0), .out1(demultiplexer_2_out1), .in(decoder_1_out1[1]), .sel(RD));  // open: en
  INDIRECT indirect_1 (.LDR(decoder_1_out2[0]), .STR(str_t), .T2(T2), .clear(indirect_1_clear), .RD(RD));
  Decoder #(.select(3)) decoder_1 (
    .out0(decoder_1_out0), .out1(decoder_1_out1[0]), .out2(decoder_1_out2[0]), .out3(str_t),
    .out4(decoder_1_out1[1]), .out5(decoder_1_out5), .out6(decoder_1_out6), .out7(out), .sel(opcode));  // open: en
  Demultiplexer #(.select(2)) demultiplexer_3 (
    .out0(T0), .out1(T1), .out2(T2), .in(1'b1), .sel(counter_1_q));  // open: out3, en
  or or_1 (or_1_out, T2, T1);
  or or_2 (or_2_out, demultiplexer_1_out0, decoder_1_out2[0], demultiplexer_2_out0);
  or or_3 (or_3_out, demultiplexer_1_out1, decoder_1_out1[0], demultiplexer_2_out1);
  and and_1 (A_enable, or_1_out, or_2_out);
  and and_2 (B_enable, or_3_out, T1);
  and and_3 (and_3_out, decoder_1_out6, T1);
  and and_4 (and_4_out, decoder_1_out5, Zero, T1);
  assign A_select = or_4_out ? {decoder_1_out1[1], decoder_1_out2[0]} : 2'bz;  // Controlled_Buffer controlled_buffer_1
  or or_4 (or_4_out, T1, T2);
  assign B_select = or_4_out ? decoder_1_out1 : 2'bz;  // Controlled_Buffer controlled_buffer_2
  or or_5 (Branch, and_3_out, and_4_out);
  ALU_control alu_control_1 (.Address(Address), .ALU_select(ALU_select), .cin(cin));
  and and_5 (str, str_t, T1);
endmodule

module ALU_control (
  input  [7:0] Address,
  output [1:0] ALU_select,
  output cin
);

  Decoder #(.select(2)) decoder_1 (
    .out1(cin), .out2(ALU_select[1]), .out3(ALU_select[0]), .sel(Address[5:4]));  // open: out0, en
endmodule

// REGISTERS
module Registers (
  input  [7:0] data,
  input  [7:0] result,
  input  [1:0] A_select,
  input  A_enable,
  input  [1:0] B_select,
  input  B_enable,
  input  T2,
  input  [11:0] instruction,
  input  TO,
  input  branch,
  input  T1,
  input  OUT,
  output [7:0] A,
  output [7:0] B,
  output [7:0] address,
  output RD,
  output [2:0] opcode,
  output [7:0] pc,
  output [7:0] buffer
);

  wire clock_1_out, or_1_out;
  wire [7:0] adder, address_t, multiplexer_1_out, multiplexer_2_out, multiplexer_3_out;

  Clock clock_1 (.out(clock_1_out));
  Multiplexer #(.select(2), .width(8)) multiplexer_1 (
    .in0(address_t), .in1(data), .in2(result), .out(multiplexer_1_out), .sel(A_select));  // open: in3, en
  Multiplexer #(.select(2), .width(8)) multiplexer_2 (
    .in0(address_t), .in1(A), .in2(result), .out(multiplexer_2_out), .sel(B_select));  // open: in3, en
  Register u_A (.D(multiplexer_1_out), .en(A_enable), .Q(A), .clk(clock_1_out));  // open: clr
  Register u_B (.D(multiplexer_2_out), .en(B_enable), .Q(B), .clk(clock_1_out));  // open: clr
  Register #(.width(12)) IR (.D(instruction), .en(TO), .Q({opcode, RD, address_t}), .clk(clock_1_out));  // open: clr
  Multiplexer #(.width(8)) multiplexer_3 (
    .in0(adder), .in1(address_t), .out(multiplexer_3_out), .sel(branch));  // open: en
  or or_1 (or_1_out, branch, T1);
  Register u_PC (.D(multiplexer_3_out), .en(or_1_out), .Q(pc), .clk(clock_1_out));  // open: clr
  Register IBR (.D(A), .en(OUT), .Q(buffer), .clk(clock_1_out));  // open: clr
  Adder adder_1 (.a(pc), .b(8'h1), .out(adder));  // open: cin, cout
  Multiplexer #(.width(8)) multiplexer_4 (.in0(address_t), .in1(A), .out(address), .sel(T2));  // open: en
endmodule

module Complementer (
  input  CIN,
  input  B0,
  input  B1,
  input  B2,
  input  B3,
  input  B4,
  input  B5,
  input  B6,
  input  B7,
  output B0_prime,
  output B1_prime,
  output B2_prime,
  output B3_prime,
  output B4_prime,
  output B5_prime,
  output B6_prime,
  output B7_prime
);

  xor xor_1 (B0_prime, CIN, B0);
  xor xor_2 (B2_prime, CIN, B2);
  xor xor_3 (B4_prime, CIN, B4);
  xor xor_4 (B6_prime, CIN, B6);
  xor xor_5 (B1_prime, CIN, B1);
  xor xor_6 (B3_prime, CIN, B3);
  xor xor_7 (B5_prime, CIN, B5);
  xor xor_8 (B7_prime, CIN, B7);
endmodule

module ALU (
  input  CIN,
  input  B0,
  input  B1,
  input  B2,
  input  B3,
  input  B4,
  input  B5,
  input  B6,
  input  B7,
  input  A0,
  input  A1,
  input  A2,
  input  A3,
  input  A4,
  input  A5,
  input  A6,
  input  A7,
  input  [1:0] selector,
  input  shift,
  output [7:0] result,
  output Zero
);

  wire [7:0] adder_1_out, and_1_out, complementer_1_b0_prime, multiplexer_1_out, multiplexer_2_out,
       shifter_1_out;

  Complementer complementer_1 (
    .CIN(CIN), .B0(B0), .B1(B1), .B2(B2), .B3(B3), .B4(B4), .B5(B5), .B6(B6), .B7(B7),
    .B0_prime(complementer_1_b0_prime[0]), .B1_prime(complementer_1_b0_prime[1]),
    .B2_prime(complementer_1_b0_prime[2]), .B3_prime(complementer_1_b0_prime[3]),
    .B4_prime(complementer_1_b0_prime[4]), .B5_prime(complementer_1_b0_prime[5]),
    .B6_prime(complementer_1_b0_prime[6]), .B7_prime(complementer_1_b0_prime[7]));
  Adder adder_1 (
    .a(complementer_1_b0_prime), .b({A7, A6, A5, A4, A3, A2, A1, A0}), .out(adder_1_out), .cin(CIN));  // open: cout
  Multiplexer #(.width(8)) multiplexer_1 (
    .in0({A7, A6, A5, A4, A3, A2, A1, A0}), .in1(complementer_1_b0_prime), .out(multiplexer_1_out),
    .sel(shift));  // open: en
  Multiplexer #(.width(8)) multiplexer_2 (
    .in0({A7, A6, A5, A4, A3, A2, A1, A0}), .in1(complementer_1_b0_prime), .out(multiplexer_2_out),
    .sel(shift));  // open: en
  assign and_1_out = complementer_1_b0_prime & {A7, A6, A5, A4, A3, A2, A1, A0};  // AND_Gate and_1, 8 bits wide
  Shifter shifter_1 (.in(multiplexer_2_out), .\dist (3'b001), .out(shifter_1_out));
  Multiplexer #(.select(2), .width(8)) multiplexer_3 (
    .in0(adder_1_out), .in1(and_1_out), .in2(shifter_1_out), .out(result), .sel(selector));  // open: in3, en
  nor nor_1 (Zero, multiplexer_1_out[0], multiplexer_1_out[1], multiplexer_1_out[2], multiplexer_1_out[3], multiplexer_1_out[4], multiplexer_1_out[5], multiplexer_1_out[6], multiplexer_1_out[7]);

  // Other names for the same wires on the sheet: select[1:0] = selector
endmodule

module INDIRECT (
  input  LDR,
  input  STR,
  input  RD,
  input  T2,
  output clear
);

  wire and_1_out, not_1_out, or_1_out;

  or or_1 (or_1_out, LDR, STR);
  not not_1 (not_1_out, and_1_out);
  and and_1 (and_1_out, or_1_out, RD);
  and and_2 (clear, not_1_out, T2);
endmodule
